// Logisim project m1_33448.circ as structural Verilog
module NOR_T (
  input  x,
  input  y,
  output z
);

  wire transistor_1_out;

  Transistor transistor_1 (.in(1'b1), .out(transistor_1_out), .gate(x));
  Transistor #(.\type ("n")) transistor_2 (.in(1'b0), .out(z), .gate(x));
  Transistor #(.\type ("n")) transistor_3 (.in(1'b0), .out(z), .gate(y));
  Transistor transistor_4 (.in(transistor_1_out), .out(z), .gate(y));
endmodule

module NOT_NOR (
  input  x,
  output y
);

  NOR_T nor_t_1 (.x(x), .y(x), .z(y));
endmodule

module OR_NOR (
  input  x,
  input  y,
  output z
);

  wire nor_t_1_z;

  NOR_T nor_t_1 (.x(x), .y(y), .z(nor_t_1_z));
  NOR_T nor_t_2 (.x(nor_t_1_z), .y(nor_t_1_z), .z(z));
endmodule

module AND_NOR (
  input  x,
  input  y,
  output z
);

  wire nor_t_1_z, nor_t_3_z;

  NOR_T nor_t_1 (.x(x), .y(x), .z(nor_t_1_z));
  NOR_T nor_t_2 (.x(nor_t_1_z), .y(nor_t_3_z), .z(z));
  NOR_T nor_t_3 (.x(y), .y(y), .z(nor_t_3_z));
endmodule

module XOR_SOP (
  input  x,
  input  y,
  output z
);

  wire and_nor_1_z, and_nor_2_z, not_nor_1_y, not_nor_2_y;

  NOT_NOR not_nor_1 (.x(x), .y(not_nor_1_y));
  AND_NOR and_nor_1 (.x(not_nor_1_y), .y(y), .z(and_nor_1_z));
  OR_NOR or_nor_1 (.x(and_nor_1_z), .y(and_nor_2_z), .z(z));
  NOT_NOR not_nor_2 (.x(y), .y(not_nor_2_y));
  AND_NOR and_nor_2 (.x(x), .y(not_nor_2_y), .z(and_nor_2_z));
endmodule

module MAJ (
  input  x,
  input  y,
  input  z,
  output out_MAJ
);

  wire and_1_out, and_2_out, and_3_out, and_4_out, not_1_out, not_2_out, not_3_out;

  not not_1 (not_1_out, x);
  not not_2 (not_2_out, y);
  not not_3 (not_3_out, z);
  and and_1 (and_1_out, z, y, not_1_out);
  and and_2 (and_2_out, x, z, not_2_out);
  and and_3 (and_3_out, x, y, not_3_out);
  and and_4 (and_4_out, x, y, z);
  or or_1 (out_MAJ, and_1_out, and_2_out, and_3_out, and_4_out);
endmodule

module ODD (
  input  x,
  input  y,
  input  z,
  output out_ODD
);

  wire and_1_out, and_2_out, and_3_out, and_4_out, not_1_out, not_2_out, not_3_out;

  not not_1 (not_1_out, x);
  not not_2 (not_2_out, y);
  not not_3 (not_3_out, z);
  and and_1 (and_1_out, not_1_out, not_2_out, z);
  and and_2 (and_2_out, not_1_out, y, not_3_out);
  and and_3 (and_3_out, x, not_2_out, not_3_out);
  and and_4 (and_4_out, x, y, z);
  or or_1 (out_ODD, and_1_out, and_2_out, and_3_out, and_4_out);
endmodule

module PESONAL_F (
  input  x,
  input  y,
  input  z,
  output Cout
);

  wire and_1_out, and_2_out, not_1_out, not_2_out, not_3_out;

  not not_1 (not_1_out, x);
  not not_2 (not_2_out, y);
  not not_3 (not_3_out, z);
  and and_1 (and_1_out, not_1_out, not_2_out, not_3_out);
  and and_2 (and_2_out, not_1_out, not_2_out, z);
  or or_1 (Cout, and_1_out, and_2_out);
endmodule

module HALF_ADDER (
  input  X,
  input  Y,
  output S,
  output C
);

  XOR_SOP xor_sop_1 (.x(X), .y(Y), .z(S));
  AND_NOR and_nor_1 (.x(X), .y(Y), .z(C));
endmodule

module FULL_ADDER_A (
  input  X,
  input  Y,
  input  CIN,
  output S,
  output COUT
);

  ODD odd_1 (.x(X), .y(Y), .z(CIN), .out_ODD(S));
  MAJ maj_1 (.x(X), .y(Y), .z(CIN), .out_MAJ(COUT));
endmodule

module FULL_ADDER_B (
  input  X,
  input  Y,
  input  CIN,
  output S,
  output COUT
);

  wire half_adder_1_c, half_adder_1_s, half_adder_2_c;

  HALF_ADDER half_adder_1 (.X(X), .Y(Y), .S(half_adder_1_s), .C(half_adder_1_c));
  OR_NOR or_nor_1 (.x(half_adder_1_c), .y(half_adder_2_c), .z(COUT));
  HALF_ADDER half_adder_2 (.X(half_adder_1_s), .Y(CIN), .S(S), .C(half_adder_2_c));
endmodule

module TESTBENCH (
  input  X,
  input  Y,
  input  CIN,
  input  in_4,
  input  in_5,
  output MISMATCH,
  output Z_T,
  output Z_REF
);

  wire [1:0] full_adder_a_1_s, full_adder_b_1_s;

  NOR_T nor_t_1 (.x(in_4), .y(in_5), .z(Z_T));
  nor NOR_BUILT_IN (Z_REF, in_4, in_5);
  FULL_ADDER_A full_adder_a_1 (.X(X), .Y(Y), .CIN(CIN), .S(full_adder_a_1_s[0]), .COUT(full_adder_a_1_s[1]));
  FULL_ADDER_B full_adder_b_1 (.X(X), .Y(Y), .CIN(CIN), .S(full_adder_b_1_s[0]), .COUT(full_adder_b_1_s[1]));
  Comparator #(.width(2)) comparator_1 (
    .a(full_adder_a_1_s), .b(full_adder_b_1_s), .gt(MISMATCH), .lt(MISMATCH));  // open: eq
endmodule
